# Fritzing sketch arduino-tp4 (saved by Fritzing 0.9.3b)
breadboards: 1

parts:
  Driver1 = 28BYJ-48 Driver Module [part_number=ULN2003 package=THT]
  SM1 = 28BYJ-48 Stepper Motor [part_number=28BYJ-48]
  Part1 = Arduino Uno (Rev3)
  R1 = PHOTOCELL [package=photocell-kit]
  R2 = Resistor [tolerance=±5% resistance=220 package=THT]
  S1 = Pushbutton [package="[THT]"]
  R3 = Resistor [tolerance=±5% resistance=220 package=THT]
  R4 = Resistor [tolerance=±5% resistance=220 package=THT]
  LED1 = LED - 5mm [color="Red (633nm)" package="5 mm [THT]"]
  LED2 = LED - 5mm [color="Blue (430nm)" package="5 mm [THT]"]
  S2 = Pushbutton [package="[THT]"]
  LED3 = LED - 5mm [color="Blue (430nm)" package="5 mm [THT]"]
  LED4 = LED - 5mm [color="Blue (430nm)" package="5 mm [THT]"]
  S3 = Pushbutton [package="[THT]"]
  S4 = Pushbutton [package="[THT]"]
  R5 = Resistor [tolerance=±5% resistance=220 package=THT]
  R6 = Resistor [tolerance=±5% resistance=220 package=THT]
  R7 = Resistor [tolerance=±5% resistance=220 package=THT]
  R8 = Resistor [tolerance=±5% resistance=220 package=THT]
  R9 = Resistor [tolerance=±5% resistance=220 package=THT]
  R10 = Resistor [tolerance=±5% resistance=220 package=THT]
  SERVO1 = Tower Pro SG90 servo [part_number=101246]
  J1 = Piezo Speaker

nets:
  N1: Driver1.IN1, Part1.D11_PWM/MOSI
  N2: Driver1.IN2, Part1.D10_PWM/SS
  N3: Driver1.IN3, Part1.D9_PWM
  N4: Driver1.IN4, Part1.D8
  GND: Driver1.GND, Part1.GND, R3.Pin_0, R4.Pin_0, R5.Pin_0, R6.Pin_0, R7.Pin_1, R8.Pin_0, R9.Pin_0, R10.Pin_0, SERVO1.GND, J1.pin1
  5V: Driver1.Vmotor, Driver1.ON/OFF-7, Part1.D1/TX, Part1.D3_PWM, Part1.D5_PWM, Part1.D7, Part1.5V, R1.P$1, S1.Pin_3, S1.Pin_4, S2.Pin_3, S2.Pin_4, S3.Pin_3, S3.Pin_4, S4.Pin_3, S4.Pin_4, SERVO1.+5V
  N5: Driver1.blue-pin, SM1.blue-pin
  N6: Driver1.pink-pin, SM1.pink-pin
  N7: Driver1.yellow-pin, SM1.yellow-pin
  N8: Driver1.orange-pin, SM1.orange-pin
  N9: Driver1.red-pin, SM1.red-pin
  N10: Part1.A0, R1.P$2, R7.Pin_0
  N11: Part1.D12/MISO, SERVO1.Signal
  N12: Part1.D13/SCK, J1.pin2
  N13: Part1.D0/RX, LED1.cathode
  N14: Part1.D2, LED2.cathode
  N15: Part1.D4, LED4.cathode
  N16: Part1.D6_PWM, LED3.cathode
  N17: R2.Pin_1, S4.Pin_1, S4.Pin_2
  N18: S1.Pin_1, S1.Pin_2, R4.Pin_1
  N19: R3.Pin_1, LED1.anode
  N20: LED2.anode, R10.Pin_1
  N21: S2.Pin_1, S2.Pin_2, R8.Pin_1
  N22: LED3.anode, R6.Pin_1
  N23: LED4.anode, R9.Pin_1
  N24: S3.Pin_1, S3.Pin_2, R5.Pin_1

custom parts:
  28BYJ-48 Driver Module: High-power ULN2003 Stepper Motor Driver Board Test Module For Arduino AVR SMD
  28BYJ-48 Stepper Motor: Unipolar Stepper Motor 28BYJ-48 Top coil - pink & orange Bottom coil - blue & yellow Common rail - red Connector pins: blue - pink - yellow - orange - red
  Tower Pro SG90 servo: Original file by John De Cristofaro http://www.adafruit.com/products/1449 Adafruit Feedback Servo (Small) Edited by: e-radionica.com 28/9/2015
